// Logisim project adder.circ as structural Verilog: 2 circuits, main circuit main
module main (
  input  [31:0] B,
  input  [31:0] A,
  input  sub,
  output ovf,
  output [31:0] result
);

  wire n1bit_adder_1_cout, n1bit_adder_2_cout, n1bit_adder_3_cout, n1bit_adder_4_cout, n1bit_adder_5_cout,
       n1bit_adder_6_cout, n1bit_adder_7_cout, n1bit_adder_8_cout, n1bit_adder_9_cout, n1bit_adder_10_cout,
       n1bit_adder_11_cout, n1bit_adder_12_cout, n1bit_adder_13_cout, n1bit_adder_14_cout,
       n1bit_adder_15_cout, n1bit_adder_16_cout, n1bit_adder_17_cout, n1bit_adder_18_cout,
       n1bit_adder_19_cout, n1bit_adder_20_cout, n1bit_adder_21_cout, n1bit_adder_22_cout,
       n1bit_adder_23_cout, n1bit_adder_24_cout, n1bit_adder_25_cout, n1bit_adder_26_cout,
       n1bit_adder_27_cout, n1bit_adder_28_cout, n1bit_adder_29_cout, n1bit_adder_30_cout,
       n1bit_adder_31_cout, n1bit_adder_32_cout, xor_2_out, xor_3_out, xor_4_out, xor_5_out, xor_6_out,
       xor_7_out, xor_8_out, xor_9_out, xor_10_out, xor_11_out, xor_12_out, xor_13_out, xor_14_out,
       xor_15_out, xor_16_out, xor_17_out, xor_18_out, xor_19_out, xor_20_out, xor_21_out, xor_22_out,
       xor_23_out, xor_24_out, xor_25_out, xor_26_out, xor_27_out, xor_28_out, xor_29_out, xor_30_out,
       xor_31_out, xor_32_out, xor_33_out;

  xor xor_1 (ovf, n1bit_adder_1_cout, n1bit_adder_2_cout);
  xor xor_2 (xor_2_out, B[31], sub);
  _1bit_adder u_1bit_adder_1 (
    .A(A[31]), .B(xor_2_out), .Cin(n1bit_adder_2_cout), .result(result[31]), .Cout(n1bit_adder_1_cout));
  xor xor_3 (xor_3_out, B[30], sub);
  _1bit_adder u_1bit_adder_2 (
    .A(A[30]), .B(xor_3_out), .Cin(n1bit_adder_3_cout), .result(result[30]), .Cout(n1bit_adder_2_cout));
  xor xor_4 (xor_4_out, B[29], sub);
  _1bit_adder u_1bit_adder_3 (
    .A(A[29]), .B(xor_4_out), .Cin(n1bit_adder_4_cout), .result(result[29]), .Cout(n1bit_adder_3_cout));
  xor xor_5 (xor_5_out, B[27], sub);
  xor xor_6 (xor_6_out, B[28], sub);
  _1bit_adder u_1bit_adder_4 (
    .A(A[28]), .B(xor_6_out), .Cin(n1bit_adder_5_cout), .result(result[28]), .Cout(n1bit_adder_4_cout));
  xor xor_7 (xor_7_out, B[26], sub);
  _1bit_adder u_1bit_adder_5 (
    .A(A[27]), .B(xor_5_out), .Cin(n1bit_adder_6_cout), .result(result[27]), .Cout(n1bit_adder_5_cout));
  _1bit_adder u_1bit_adder_6 (
    .A(A[26]), .B(xor_7_out), .Cin(n1bit_adder_7_cout), .result(result[26]), .Cout(n1bit_adder_6_cout));
  xor xor_8 (xor_8_out, B[25], sub);
  _1bit_adder u_1bit_adder_7 (
    .A(A[25]), .B(xor_8_out), .Cin(n1bit_adder_8_cout), .result(result[25]), .Cout(n1bit_adder_7_cout));
  xor xor_9 (xor_9_out, B[24], sub);
  _1bit_adder u_1bit_adder_8 (
    .A(A[24]), .B(xor_9_out), .Cin(n1bit_adder_9_cout), .result(result[24]), .Cout(n1bit_adder_8_cout));
  xor xor_10 (xor_10_out, B[23], sub);
  _1bit_adder u_1bit_adder_9 (
    .A(A[23]), .B(xor_10_out), .Cin(n1bit_adder_10_cout), .result(result[23]), .Cout(n1bit_adder_9_cout));
  xor xor_11 (xor_11_out, B[22], sub);
  _1bit_adder u_1bit_adder_10 (
    .A(A[22]), .B(xor_11_out), .Cin(n1bit_adder_11_cout), .result(result[22]), .Cout(n1bit_adder_10_cout));
  xor xor_12 (xor_12_out, B[21], sub);
  xor xor_13 (xor_13_out, B[20], sub);
  _1bit_adder u_1bit_adder_11 (
    .A(A[21]), .B(xor_12_out), .Cin(n1bit_adder_13_cout), .result(result[21]), .Cout(n1bit_adder_11_cout));
  xor xor_14 (xor_14_out, B[19], sub);
  _1bit_adder u_1bit_adder_12 (
    .A(A[19]), .B(xor_14_out), .Cin(n1bit_adder_14_cout), .result(result[19]), .Cout(n1bit_adder_12_cout));
  _1bit_adder u_1bit_adder_13 (
    .A(A[20]), .B(xor_13_out), .Cin(n1bit_adder_12_cout), .result(result[20]), .Cout(n1bit_adder_13_cout));
  xor xor_15 (xor_15_out, B[18], sub);
  _1bit_adder u_1bit_adder_14 (
    .A(A[18]), .B(xor_15_out), .Cin(n1bit_adder_15_cout), .result(result[18]), .Cout(n1bit_adder_14_cout));
  xor xor_16 (xor_16_out, B[17], sub);
  _1bit_adder u_1bit_adder_15 (
    .A(A[17]), .B(xor_16_out), .Cin(n1bit_adder_16_cout), .result(result[17]), .Cout(n1bit_adder_15_cout));
  xor xor_17 (xor_17_out, B[16], sub);
  _1bit_adder u_1bit_adder_16 (
    .A(A[16]), .B(xor_17_out), .Cin(n1bit_adder_17_cout), .result(result[16]), .Cout(n1bit_adder_16_cout));
  xor xor_18 (xor_18_out, B[15], sub);
  _1bit_adder u_1bit_adder_17 (
    .A(A[15]), .B(xor_18_out), .Cin(n1bit_adder_18_cout), .result(result[15]), .Cout(n1bit_adder_17_cout));
  xor xor_19 (xor_19_out, B[14], sub);
  xor xor_20 (xor_20_out, B[13], sub);
  _1bit_adder u_1bit_adder_18 (
    .A(A[14]), .B(xor_19_out), .Cin(n1bit_adder_20_cout), .result(result[14]), .Cout(n1bit_adder_18_cout));
  xor xor_21 (xor_21_out, B[12], sub);
  _1bit_adder u_1bit_adder_19 (
    .A(A[12]), .B(xor_21_out), .Cin(n1bit_adder_21_cout), .result(result[12]), .Cout(n1bit_adder_19_cout));
  _1bit_adder u_1bit_adder_20 (
    .A(A[13]), .B(xor_20_out), .Cin(n1bit_adder_19_cout), .result(result[13]), .Cout(n1bit_adder_20_cout));
  xor xor_22 (xor_22_out, B[11], sub);
  _1bit_adder u_1bit_adder_21 (
    .A(A[11]), .B(xor_22_out), .Cin(n1bit_adder_22_cout), .result(result[11]), .Cout(n1bit_adder_21_cout));
  xor xor_23 (xor_23_out, B[10], sub);
  _1bit_adder u_1bit_adder_22 (
    .A(A[10]), .B(xor_23_out), .Cin(n1bit_adder_23_cout), .result(result[10]), .Cout(n1bit_adder_22_cout));
  xor xor_24 (xor_24_out, B[9], sub);
  _1bit_adder u_1bit_adder_23 (
    .A(A[9]), .B(xor_24_out), .Cin(n1bit_adder_24_cout), .result(result[9]), .Cout(n1bit_adder_23_cout));
  xor xor_25 (xor_25_out, B[8], sub);
  _1bit_adder u_1bit_adder_24 (
    .A(A[8]), .B(xor_25_out), .Cin(n1bit_adder_25_cout), .result(result[8]), .Cout(n1bit_adder_24_cout));
  xor xor_26 (xor_26_out, B[7], sub);
  _1bit_adder u_1bit_adder_25 (
    .A(A[7]), .B(xor_26_out), .Cin(n1bit_adder_26_cout), .result(result[7]), .Cout(n1bit_adder_25_cout));
  xor xor_27 (xor_27_out, B[6], sub);
  xor xor_28 (xor_28_out, B[5], sub);
  _1bit_adder u_1bit_adder_26 (
    .A(A[6]), .B(xor_27_out), .Cin(n1bit_adder_28_cout), .result(result[6]), .Cout(n1bit_adder_26_cout));
  xor xor_29 (xor_29_out, B[4], sub);
  _1bit_adder u_1bit_adder_27 (
    .A(A[4]), .B(xor_29_out), .Cin(n1bit_adder_29_cout), .result(result[4]), .Cout(n1bit_adder_27_cout));
  _1bit_adder u_1bit_adder_28 (
    .A(A[5]), .B(xor_28_out), .Cin(n1bit_adder_27_cout), .result(result[5]), .Cout(n1bit_adder_28_cout));
  xor xor_30 (xor_30_out, B[3], sub);
  _1bit_adder u_1bit_adder_29 (
    .A(A[3]), .B(xor_30_out), .Cin(n1bit_adder_30_cout), .result(result[3]), .Cout(n1bit_adder_29_cout));
  xor xor_31 (xor_31_out, B[2], sub);
  _1bit_adder u_1bit_adder_30 (
    .A(A[2]), .B(xor_31_out), .Cin(n1bit_adder_31_cout), .result(result[2]), .Cout(n1bit_adder_30_cout));
  xor xor_32 (xor_32_out, B[1], sub);
  _1bit_adder u_1bit_adder_31 (
    .A(A[1]), .B(xor_32_out), .Cin(n1bit_adder_32_cout), .result(result[1]), .Cout(n1bit_adder_31_cout));
  xor xor_33 (xor_33_out, B[0], sub);
  _1bit_adder u_1bit_adder_32 (.A(A[0]), .B(xor_33_out), .Cin(sub), .result(result[0]), .Cout(n1bit_adder_32_cout));
endmodule

module _1bit_adder (
  input  A,
  input  B,
  input  Cin,
  output result,
  output Cout
);

  wire and_1_out, and_2_out, xor_1_out;

  xor xor_1 (xor_1_out, A, B);
  xor xor_2 (result, xor_1_out, Cin);
  and and_1 (and_1_out, Cin, xor_1_out);
  and and_2 (and_2_out, B, A);
  or or_1 (Cout, and_1_out, and_2_out);
endmodule
