// Logisim project circuit1.circ as structural Verilog: 1 circuit, main circuit main
module main (
  input  A,
  input  B,
  input  C,
  output out
);

  wire and_1_out, and_2_out, not_1_out, not_2_out, or_1_out;

  or or_1 (or_1_out, A, B);
  not not_1 (not_1_out, B);
  not not_2 (not_2_out, C);
  and and_1 (and_1_out, not_1_out, C);
  and and_2 (and_2_out, or_1_out, not_2_out);
  or or_2 (out, and_2_out, and_2_out, and_1_out);
endmodule
