// Logisim project fsm.circ as structural Verilog: 5 circuits, main circuit main
module main (
  input  in1,
  input  in2,
  input  in3,
  output out1,
  output out2
);

  wire clock_1_out;

  Clock clock_1 (.out(clock_1_out));
  out1 out1_1 (.in1(in1), .in2(in2), .in3(in3), .clk(clock_1_out), .out1(out1));
  out2 out2_1 (.in1(in1), .in2(in2), .in3(in3), .clk(clock_1_out), .out2(out2));
endmodule

module out1 (
  input  in1,
  input  in2,
  input  in3,
  input  clk,
  output out1
);

  wire trueorfalse_1_val;

  trueOrFalse trueorfalse_1 (.i1(in1), .i2(in2), .i3(in3), .val(trueorfalse_1_val));
  D_Flip_Flop d_ff_1 (.clk(clk), .D(trueorfalse_1_val), .Q(out1));  // open: Qn, preset, en, reset
endmodule

module trueOrFalse (
  input  i1,
  input  i2,
  input  i3,
  output val
);

  wire and_1_out, and_2_out, and_3_out, not_1_out, not_2_out, not_3_out;

  not not_1 (not_1_out, i1);
  not not_2 (not_2_out, i2);
  not not_3 (not_3_out, i3);
  and and_1 (and_1_out, not_1_out, i2, i3);
  and and_2 (and_2_out, i1, not_2_out, i3);
  and and_3 (and_3_out, i1, i2, not_3_out);
  or or_1 (val, and_1_out, and_2_out, and_3_out);
endmodule

module out2 (
  input  in1,
  input  in2,
  input  in3,
  input  clk,
  output out2
);

  wire out2_truefalse_1_val, State1_q;

  out2_trueFalse out2_truefalse_1 (.i1(in1), .i2(in2), .i3(in3), .val(out2_truefalse_1_val));
  D_Flip_Flop State1 (.clk(clk), .D(out2_truefalse_1_val), .Q(State1_q));  // open: Qn, preset, en, reset
  D_Flip_Flop State2 (.clk(clk), .D(State1_q), .Q(out2));  // open: Qn, preset, en, reset
endmodule

module out2_trueFalse (
  input  i1,
  input  i2,
  input  i3,
  output val
);

  wire and_1_out, and_2_out, and_3_out, not_1_out, not_2_out, not_3_out, not_4_out, not_5_out, not_6_out;

  not not_1 (not_1_out, i1);
  not not_2 (not_2_out, i2);
  not not_3 (not_3_out, i1);
  not not_4 (not_4_out, i3);
  not not_5 (not_5_out, i2);
  not not_6 (not_6_out, i3);
  and and_1 (and_1_out, not_1_out, not_2_out, i3);
  and and_2 (and_2_out, not_3_out, i2, not_4_out);
  and and_3 (and_3_out, i1, not_5_out, not_6_out);
  or or_1 (val, and_1_out, and_2_out, and_3_out);
endmodule
